# Fritzing sketch swift (saved by Fritzing 0.9.3b)
breadboards: 1

parts:
  Part1 = PocketBeagle
  U1 = 74HC595 [package="DIP16 [THT]"]
  Q1 = TRANSISTOR_NPN [package=to-92-ammo]
  Q2 = TRANSISTOR_NPN [package=to-92-ammo]
  Q3 = TRANSISTOR_NPN [package=to-92-ammo]
  LED1 = LEDs [package=led10mm]
  LED2 = LEDs [package=led10mm]
  LED3 = LEDs [package=led10mm]
  LED4 = LEDs [package=led10mm]
  LED5 = LEDs [package=led10mm]
  LED6 = LEDs [package=led10mm]
  LED7 = LEDs [package=led10mm]

nets:
  N1: Part1.PRU0.7, Q1.B
  N2: Part1.PRU0.4, Q3.B
  N3: Part1.PRU0.1, Q2.B
  N4: U1.Q1, LED1.A
  N5: U1.Q2, LED5.A
  N6: U1.Q3, LED4.A
  N7: U1.Q4, LED3.A
  N8: U1.Q5, U1.GND, LED1.C, LED2.C, LED2.A, LED3.C, LED4.C, LED5.C, LED6.C
  N9: U1.Q7, LED6.A
  N10: U1.MR, U1.VCC, Q1.C, Q2.C, Q3.C
  N11: U1.SH_CP, Q2.E
  N12: U1.ST_CP, Q3.E
  N13: U1.OE, LED7.C
  N14: U1.DS, Q1.E
  N15: U1.Q0, LED7.A
