# Fritzing sketch 74hc299_10 (saved by Fritzing 0.9.3b)
breadboards: 1

parts:
  Part3 = TXB0108 8-channel Bi-directional Logic Level Converter
  BeagleBone1 = BeagleBone Black
  IC1 = IC, DIP package, 20 pins [chip_label=54HC299]
  R9 = Resistor [tolerance=±5% resistance=10k package="2512 [SMD]"]
  LED1 = LED - 3mm [color="Yellow (592nm)" package="3 mm [THT]"]
  LED3 = LED - 3mm [color="Red (633nm)" package="3 mm [THT]"]
  LED4 = LED - 3mm [color="Red (633nm)" package="3 mm [THT]"]
  R10 = Resistor [tolerance=±5% resistance=220 package="2512 [SMD]"]
  R11 = Resistor [tolerance=±5% resistance=220 package="2512 [SMD]"]
  R12 = Resistor [tolerance=±5% resistance=220 package="2512 [SMD]"]
  R13 = Resistor [tolerance=±5% resistance=220 package="2512 [SMD]"]
  LED5 = LED - 3mm [color="Blue (430nm)" package="3 mm [THT]"]
  LED6 = LED - 3mm [color="Blue (430nm)" package="3 mm [THT]"]
  R14 = Resistor [tolerance=±5% resistance=220 package="2512 [SMD]"]

nets:
  N1: Part3.B1, IC1.pin19, R14.Pin_1
  N2: Part3.B2, IC1.pin1, R13.Pin_1
  N3: Part3.B3, IC1.pin2
  N4: Part3.B4, IC1.pin3
  N5: Part3.B5, IC1.pin11, R11.Pin_1
  N6: Part3.B6, IC1.pin12, R12.Pin_1
  N7: Part3.B8, R10.Pin_1
  N8: Part3.GND, Part3.A4, Part3.A3, BeagleBone1.no_name_yet#102, IC1.pin10, LED1.cathode, LED3.cathode, LED4.cathode, LED5.cathode, LED6.cathode
  N9: Part3.OE, R9.Pin_1
  N10: Part3.A8, BeagleBone1.no_name_yet#120
  N11: Part3.A7, BeagleBone1.no_name_yet#104
  N12: Part3.A6, BeagleBone1.no_name_yet#116
  N13: Part3.A5, BeagleBone1.no_name_yet#103
  N14: Part3.A2, BeagleBone1.no_name_yet#112
  N15: Part3.A1, BeagleBone1.no_name_yet#111
  N16: Part3.VCCA, BeagleBone1.no_name_yet#4
  N17: BeagleBone1.no_name_yet#8, IC1.pin9, IC1.pin20, R9.Pin_0
  N18: LED1.anode, R10.Pin_0
  N19: LED3.anode, R11.Pin_0
  N20: LED4.anode, R12.Pin_0
  N21: R13.Pin_0, LED5.anode
  N22: LED6.anode, R14.Pin_0

notes:
  54hc299 shift register cascaded interface with Beagle Bone Black
  4-bit Output to logic analyzer
  4-bit Input
  |-8-bit-|
  S0          S1        CHK LED   DATA IN      CP

custom parts:
  TXB0108 8-channel Bi-directional Logic Level Converter: Because the Arduino (and Basic Stamp) are 5V devices, and most modern sensors, displays, flash cards and modes are 3.3V-only, many makers find that they need to perform level shifting/conversion to protect the 3.3V device from 5V. Although one can use resistors to make a divider, for high speed transfers, the resistors can add a lot of slew and cause havoc that is tough to debug. For that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
  BeagleBone Black: BeagleBone Black rev. A5B
