# Fritzing sketch swift_bi (saved by Fritzing 0.9.3b)
breadboards: 2

parts:
  Part3 = TXB0108 8-channel Bi-directional Logic Level Converter
  IC2 = IC, DIP package, 20 pins [chip_label=54HC299]
  BeagleBone1 = BeagleBone Black
  IC1 = IC, DIP package, 20 pins [chip_label=54HC299]
  S1 = Pushbutton [package="[SMD]"]
  R1 = Resistor [tolerance=±5% resistance=10k package="2512 [SMD]"]
  S2 = Pushbutton [package="[SMD]"]
  R2 = Resistor [tolerance=±5% resistance=10k package="2512 [SMD]"]
  S3 = Pushbutton [package="[SMD]"]
  R3 = Resistor [tolerance=±5% resistance=10k package="2512 [SMD]"]
  S4 = Pushbutton [package="[SMD]"]
  R4 = Resistor [tolerance=±5% resistance=10k package="2512 [SMD]"]
  S5 = Pushbutton [package="[SMD]"]
  R5 = Resistor [tolerance=±5% resistance=10k package="2512 [SMD]"]
  S6 = Pushbutton [package="[SMD]"]
  R6 = Resistor [tolerance=±5% resistance=10k package="2512 [SMD]"]
  S7 = Pushbutton [package="[SMD]"]
  R7 = Resistor [tolerance=±5% resistance=10k package="2512 [SMD]"]
  S8 = Pushbutton [package="[SMD]"]
  R8 = Resistor [tolerance=±5% resistance=10k package="2512 [SMD]"]
  R9 = Resistor [tolerance=±5% resistance=10k package="2512 [SMD]"]
  LED1 = LED - 3mm [color="Yellow (592nm)" package="3 mm [THT]"]
  LED3 = LED - 3mm [color="Red (633nm)" package="3 mm [THT]"]
  LED4 = LED - 3mm [color="Red (633nm)" package="3 mm [THT]"]
  R10 = Resistor [tolerance=±5% resistance=220 package="2512 [SMD]"]
  R11 = Resistor [tolerance=±5% resistance=220 package="2512 [SMD]"]
  R12 = Resistor [tolerance=±5% resistance=220 package="2512 [SMD]"]

nets:
  N1: Part3.B1, IC2.pin19, IC1.pin19
  N2: Part3.B2, IC2.pin1, IC1.pin1
  N3: Part3.B3, IC2.pin2, IC1.pin2
  N4: Part3.B4, IC2.pin3, IC1.pin3
  N5: Part3.B5, IC1.pin11, R11.Pin_1
  N6: Part3.B6, IC2.pin12, IC1.pin12, R12.Pin_1
  N7: Part3.B7, IC2.pin17
  N8: Part3.B8, R10.Pin_1
  N9: Part3.GND, Part3.A4, Part3.A3, IC2.pin10, BeagleBone1.no_name_yet#102, IC1.pin10, R1.Pin_0, R2.Pin_0, R3.Pin_0, R4.Pin_0, R5.Pin_0, R6.Pin_0, R7.Pin_0, R8.Pin_0, LED1.cathode, LED3.cathode, LED4.cathode
  N10: Part3.OE, R9.Pin_1
  N11: Part3.A8, BeagleBone1.no_name_yet#120
  N12: Part3.A7, BeagleBone1.no_name_yet#104
  N13: Part3.A6, BeagleBone1.no_name_yet#116
  N14: Part3.A5, BeagleBone1.no_name_yet#103
  N15: Part3.A2, BeagleBone1.no_name_yet#112
  N16: Part3.A1, BeagleBone1.no_name_yet#111
  N17: Part3.VCCA, BeagleBone1.no_name_yet#4
  N18: IC2.pin4, S7.Pin_1, S7.Pin_2, R7.Pin_1
  N19: IC2.pin5, S5.Pin_1, S5.Pin_2, R5.Pin_1
  N20: IC2.pin6, S3.Pin_1, S3.Pin_2, R3.Pin_1
  N21: IC2.pin7, S1.Pin_1, S1.Pin_2, R1.Pin_1
  N22: IC2.pin11, IC1.pin17
  N23: IC2.pin13, S8.Pin_1, S8.Pin_2, R8.Pin_1
  N24: IC2.pin14, S6.Pin_1, S6.Pin_2, R6.Pin_1
  N25: IC2.pin15, S4.Pin_1, S4.Pin_2, R4.Pin_1
  N26: IC2.pin16, S2.Pin_1, S2.Pin_2, R2.Pin_1
  N27: IC2.pin20, BeagleBone1.no_name_yet#8, IC1.pin9, IC1.pin20, S1.Pin_3, S1.Pin_4, S2.Pin_3, S2.Pin_4, S3.Pin_3, S3.Pin_4, S4.Pin_3, S4.Pin_4, S5.Pin_3, S5.Pin_4, S6.Pin_3, S6.Pin_4, S7.Pin_3, S7.Pin_4, S8.Pin_3, S8.Pin_4, R9.Pin_0
  N28: LED1.anode, R10.Pin_0
  N29: LED3.anode, R11.Pin_0
  N30: LED4.anode, R12.Pin_0

notes:
  54hc299 shift register cascaded interface with Beagle Bone Black
  4-bit Output to logic analyzer
  4-bit input
  4-bit Input
  |-8-bit-|
  |-----------16-bit-------------|
  CHK LED   DATA IN    CP
  0  1  2  3  4  5  6  7

custom parts:
  TXB0108 8-channel Bi-directional Logic Level Converter: Because the Arduino (and Basic Stamp) are 5V devices, and most modern sensors, displays, flash cards and modes are 3.3V-only, many makers find that they need to perform level shifting/conversion to protect the 3.3V device from 5V. Although one can use resistors to make a divider, for high speed transfers, the resistors can add a lot of slew and cause havoc that is tough to debug. For that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
  BeagleBone Black: BeagleBone Black rev. A5B
