# Fritzing sketch switch_bbb (saved by Fritzing 0.9.3b)
circuit board: 6.88176cm x 9.61717cm
breadboards: 3

parts:
  R10 = Resistor [resistance=220 tolerance=±5% package=THT]
  R11 = Resistor [resistance=220 tolerance=±5% package=THT]
  R13 = Resistor [resistance=220 tolerance=±5% package=THT]
  LED10 = LED - 5mm [color="Blue (470nm)" package="5 mm [THT]"]
  LED11 = LED - 5mm [color="Red (633nm)" package="5 mm [THT]"]
  LED14 = LED - 5mm [color="Yellow (592nm)" package="5 mm [THT]"]
  Part3 = TXB0108 8-channel Bi-directional Logic Level Converter
  BeagleBone1 = BeagleBone Black
  R26 = Resistor [tolerance=±5% resistance=10k package=THT]
  R27 = Resistor [tolerance=±5% resistance=10k package="0402 [SMD]"]
  S1 = Momentary Switch [package=ksa_sealed_tac_switch]
  Q1 = PNP-Transistor [package="TO92 [THT]"]
  Q2 = PNP-Transistor [package="TO92 [THT]"]
  Q3 = PNP-Transistor [package="TO92 [THT]"]

nets:
  N1: R10.Pin_0, LED14.anode
  N2: R10.Pin_1, Q2.E
  N3: R11.Pin_0, LED10.anode
  N4: R11.Pin_1, Q3.E
  N5: R13.Pin_0, LED11.anode
  N6: R13.Pin_1, Q1.E
  N7: LED10.cathode, LED11.cathode, LED14.cathode, Part3.GND, BeagleBone1.no_name_yet#102, R27.Pin_1
  N8: Part3.VCCB, BeagleBone1.no_name_yet#6, Q1.B, Q2.B, Q3.B
  N9: Part3.B1, S1.4
  N10: Part3.OE, R26.Pin_0
  N11: Part3.A1, BeagleBone1.no_name_yet#111
  N12: Part3.VCCA, BeagleBone1.no_name_yet#4, R26.Pin_1
  N13: BeagleBone1.no_name_yet#103, Q3.C
  N14: BeagleBone1.no_name_yet#112, Q2.C
  N15: BeagleBone1.no_name_yet#115, Q1.C
  N16: R27.Pin_0, S1.2

notes:
  In this project, one 74HC595 shift register are used to control 8 LEDs with just 5 BB Black
  pins through assembly code of pru.
  Related example: https://github.com/pranav083/pocket_beagle-work/

custom parts:
  TXB0108 8-channel Bi-directional Logic Level Converter: Because the Arduino (and Basic Stamp) are 5V devices, and most modern sensors, displays, flash cards and modes are 3.3V-only, many makers find that they need to perform level shifting/conversion to protect the 3.3V device from 5V. Although one can use resistors to make a divider, for high speed transfers, the resistors can add a lot of slew and cause havoc that is tough to debug. For that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
  BeagleBone Black: BeagleBone Black rev. A5B

// code stored in the sketch: Shift_Register_2x.ino
//**************************************************************//
//  Name    : shiftOutCode, Dual One By One                           //
//  Author  : Carlyn Maw, Tom Igoe                               //
//  Date    : 25 Oct, 2006                                       //
//  Version : 1.0                                                //
//  Notes   : Code for using a 74HC595 Shift Register            //
//          : to count from 0 to 255                             //
//**************************************************************//

//Pin connected to ST_CP of 74HC595
int latchPin = 8;
//Pin connected to SH_CP of 74HC595
int clockPin = 12;
////Pin connected to DS of 74HC595
int dataPin = 11;

//holder for infromation you're going to pass to shifting function
byte data = 0; 



void setup() {
  //set pins to output because they are addressed in the main loop
  pinMode(latchPin, OUTPUT);

}

void loop() {

  //function that blinks all the LEDs
  //gets passed the number of blinks and the pause time
  blinkAll_2Bytes(1,500); 

  // light each pin one by one using a function A
  for (int j = 0; j < 8; j++) {
    //ground latchPin and hold low for as long as you are transmitting
    digitalWrite(latchPin, 0);
    //red LEDs
    lightShiftPinA(7-j);
    //green LEDs
    lightShiftPinA(j);
    //return the latch pin high to signal chip that it 
    //no longer needs to listen for information
    digitalWrite(latchPin, 1);
    delay(1000);
  }

  // light each pin one by one using a function A
  for (int j = 0; j < 8; j++) {
    //ground latchPin and hold low for as long as you are transmitting
    digitalWrite(latchPin, 0);
    //red LEDs
    lightShiftPinB(j);
    //green LEDs
    lightShiftPinB(7-j);
    //return the latch pin high to signal chip that it 
    //no longer needs to listen for information
    digitalWrite(latchPin, 1);
    delay(1000);
  } 

}

//This function uses bitwise math to move the pins up
void lightShiftPinA(int p) {
  //defines a local variable
  int pin;

  //this is line uses a bitwise operator
  //shifting a bit left using << is the same
  //as multiplying the decimal number by two. 
  pin = 1<< p;

  //move 'em out
  shiftOut(dataPin, clockPin, pin);   

}

//This function uses that fact that each bit in a byte
//is 2 times greater than the one before it to
//shift the bits higher
void lightShiftPinB(int p) {
  //defines a local variable
  int pin;

  //start with the pin = 1 so that if 0 is passed to this
  //function pin 0 will light. 
  pin = 1;

  for (int x = 0; x < p; x++) {
    pin = pin * 2; 
  }
  //move 'em out
  shiftOut(dataPin, clockPin, pin);   
}


// the heart of the program
void shiftOut(int myDataPin, int myClockPin, byte myDataOut) {
  // This shifts 8 bits out MSB first, 
  //on the rising edge of the clock,
  //clock idles low

  //internal function setup
  int i=0;
  int pinState;
  pinMode(myClockPin, OUTPUT);
  pinMode(myDataPin, OUTPUT);

  //clear everything out just in case to
  //prepare shift register for bit shifting
  digitalWrite(myDataPin, 0);
  digitalWrite(myClockPin, 0);

  //for each bit in the byte myDataOut?
  //NOTICE THAT WE ARE COUNTING DOWN in our for loop
  //This means that %00000001 or "1" will go through such
  //that it will be pin Q0 that lights. 
  for (i=7; i>=0; i--)  {
    digitalWrite(myClockPin, 0);

    //if the value passed to myDataOut and a bitmask result 
    // true then... so if we are at i=6 and our value is
    // %11010100 it would the code compares it to %01000000 
    // and proceeds to set pinState to 1.
    if ( myDataOut & (1<<i) ) {
      pinState= 1;
    }
    else {	
      pinState= 0;
    }

    //Sets the pin to HIGH or LOW depending on pinState
    digitalWrite(myDataPin, pinState);
    //register shifts bits on upstroke of clock pin  
    digitalWrite(myClockPin, 1);
    //zero the data pin after shift to prevent bleed through
    digitalWrite(myDataPin, 0);
  }

  //stop shifting
  digitalWrite(myClockPin, 0);
}


//blinks both registers based on the number of times you want to 
//blink "n" and the pause between them "d"
//starts with a moment of darkness to make sure the first blink
//has its full visual effect.
void blinkAll_2Bytes(int n, int d) {
  digitalWrite(latchPin, 0);
  shiftOut(dataPin, clockPin, 0);
  shiftOut(dataPin, clockPin, 0);
  digitalWrite(latchPin, 1);
  delay(200);
  for (int x = 0; x < n; x++) {
    digitalWrite(latchPin, 0);
    shiftOut(dataPin, clockPin, 255);
    shiftOut(dataPin, clockPin, 255);
    digitalWrite(latchPin, 1);
    delay(d);
    digitalWrite(latchPin, 0);
    shiftOut(dataPin, clockPin, 0);
    shiftOut(dataPin, clockPin, 0);
    digitalWrite(latchPin, 1);
    delay(d);
  }
}
