# Fritzing sketch swift_bi_lcd (saved by Fritzing 0.9.3b)
breadboards: 2

parts:
  Part1 = PocketBeagle
  Part3 = TXB0108 8-channel Bi-directional Logic Level Converter
  IC1 = IC, DIP package, 20 pins [chip_label=54HC299]
  5v_power_supply = Power plug
  16x2_LCD_Display = LCD-16X2 [package=lcd-16x2]
  R1 = Trimmer Potentiometer [maximum_resistance=10kΩ package=THT]

nets:
  VIN: Part1.VIN, IC1.pin20, 5v_power_supply.VCC, 16x2_LCD_Display.VDD, 16x2_LCD_Display.A, R1.leg2
  GND: Part1.GND, Part3.GND, IC1.pin10, 5v_power_supply.GND, R1.leg1
  N1: Part1.GPIO59, Part3.A1
  N2: Part1.GPIO58, Part3.A2
  N3: Part1.GPIO57, Part3.A3
  N4: Part1.GPIO60, Part3.A4
  N5: Part1.GPIO52, Part3.A5
  N6: Part1.GPIO65, Part3.A7
  N7: Part1.GPIO64, Part3.A6
  N8: Part1.3.3V, Part3.VCCA
  N9: Part3.B1, IC1.pin19
  N10: Part3.B2, IC1.pin1
  N11: Part3.B3, IC1.pin2
  N12: Part3.B4, IC1.pin3
  N13: Part3.B5, IC1.pin11
  N14: Part3.B6, IC1.pin12
  N15: Part3.B7, IC1.pin9
  N16: IC1.pin5, 16x2_LCD_Display.E
  N17: IC1.pin6, 16x2_LCD_Display.DB5
  N18: IC1.pin7, 16x2_LCD_Display.RS
  N19: IC1.pin13, 16x2_LCD_Display.DB4
  N20: IC1.pin14, 16x2_LCD_Display.DB6
  N21: IC1.pin15, 16x2_LCD_Display.DB7
  N22: 16x2_LCD_Display.VSS, 16x2_LCD_Display.R_W, 16x2_LCD_Display.K
  N23: 16x2_LCD_Display.VO, R1.wiper

notes:
  54hc299 shift register and lcd interface with Pocket beagle
  |-8-bit-|
  Data line

custom parts:
  TXB0108 8-channel Bi-directional Logic Level Converter: Because the Arduino (and Basic Stamp) are 5V devices, and most modern sensors, displays, flash cards and modes are 3.3V-only, many makers find that they need to perform level shifting/conversion to protect the 3.3V device from 5V. Although one can use resistors to make a divider, for high speed transfers, the resistors can add a lot of slew and cause havoc that is tough to debug. For that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
