# Fritzing sketch swift_7se (saved by Fritzing 0.9.3b)
breadboards: 2

parts:
  Part1 = PocketBeagle
  Part3 = TXB0108 8-channel Bi-directional Logic Level Converter
  IC1 = IC, DIP package, 20 pins [chip_label=54HC299]
  IC2 = IC, DIP package, 20 pins [chip_label=54HC299]
  IC3 = IC, DIP package, 20 pins [chip_label=54HC299]
  IC4 = IC, DIP package, 20 pins [chip_label=54HC299]
  5v_power_supply = Power plug
  7_Segment11 = 7 Segment Display
  7_Segment12 = 7 Segment Display
  7_Segment13 = 7 Segment Display
  7_Segment14 = 7 Segment Display

nets:
  VIN: Part1.VIN, IC1.pin20, IC2.pin20, IC3.pin20, IC4.pin20, 5v_power_supply.VCC, 7_Segment11.common_anode, 7_Segment12.common_anode, 7_Segment13.common_anode, 7_Segment14.common_anode
  N1: Part1.GPIO59, Part3.A1
  N2: Part1.GPIO58, Part3.A2
  N3: Part1.GPIO57, Part3.A3
  N4: Part1.GPIO60, Part3.A4
  N5: Part1.GPIO52, Part3.A5
  GND: Part1.GND, Part3.GND, IC1.pin10, IC2.pin10, IC3.pin10, IC4.pin10, 5v_power_supply.GND
  N6: Part1.GPIO65, Part3.A7
  N7: Part1.GPIO64, Part3.A6
  N8: Part1.3.3V, Part3.VCCA
  N9: Part3.B1, IC1.pin19, IC2.pin19, IC3.pin19, IC4.pin19
  N10: Part3.B2, IC1.pin1, IC2.pin1, IC3.pin1, IC4.pin1
  N11: Part3.B3, IC1.pin2, IC2.pin2, IC3.pin2, IC4.pin2
  N12: Part3.B4, IC1.pin3, IC2.pin3, IC3.pin3, IC4.pin3
  N13: Part3.B5, IC1.pin11
  N14: Part3.B6, IC1.pin12, IC2.pin12, IC3.pin12, IC4.pin12
  N15: Part3.B7, IC1.pin9, IC2.pin9, IC4.pin9
  N16: IC1.pin4, 7_Segment11.Segment_A
  N17: IC1.pin5, 7_Segment11.Segment_B
  N18: IC1.pin6, 7_Segment11.Segment_C
  N19: IC1.pin7, 7_Segment11.Segment_DP
  N20: IC1.pin8, IC2.pin18
  N21: IC1.pin13, 7_Segment11.Segment_D
  N22: IC1.pin14, 7_Segment11.Segment_E
  N23: IC1.pin15, 7_Segment11.Segment_F
  N24: IC1.pin16, 7_Segment11.Segment_G
  N25: IC1.pin17, IC2.pin11
  N26: IC2.pin4, 7_Segment12.Segment_A
  N27: IC2.pin5, 7_Segment12.Segment_B
  N28: IC2.pin6, 7_Segment12.Segment_C
  N29: IC2.pin7, 7_Segment12.Segment_DP
  N30: IC2.pin8, IC3.pin18
  N31: IC2.pin13, 7_Segment12.Segment_D
  N32: IC2.pin14, 7_Segment12.Segment_E
  N33: IC2.pin15, 7_Segment12.Segment_F
  N34: IC2.pin16, 7_Segment12.Segment_G
  N35: IC2.pin17, IC3.pin11
  N36: IC3.pin4, 7_Segment14.Segment_A
  N37: IC3.pin5, 7_Segment14.Segment_B
  N38: IC3.pin6, 7_Segment14.Segment_C
  N39: IC3.pin7, 7_Segment14.Segment_DP
  N40: IC3.pin8, IC4.pin18
  N41: IC3.pin13, 7_Segment14.Segment_D
  N42: IC3.pin14, 7_Segment14.Segment_E
  N43: IC3.pin15, 7_Segment14.Segment_F
  N44: IC3.pin16, 7_Segment14.Segment_G
  N45: IC3.pin17, IC4.pin11
  N46: IC4.pin4, 7_Segment13.Segment_A
  N47: IC4.pin5, 7_Segment13.Segment_B
  N48: IC4.pin6, 7_Segment13.Segment_C
  N49: IC4.pin7, 7_Segment13.Segment_DP
  N50: IC4.pin13, 7_Segment13.Segment_D
  N51: IC4.pin14, 7_Segment13.Segment_E
  N52: IC4.pin15, 7_Segment13.Segment_F
  N53: IC4.pin16, 7_Segment13.Segment_G

notes:
  54hc299 shift register and seven segment display interface with Pocket beagle
  |-8-bit-|
  |-----------------------------------32-bit----------------------------- |
  |-----------16-bit-------------|

custom parts:
  TXB0108 8-channel Bi-directional Logic Level Converter: Because the Arduino (and Basic Stamp) are 5V devices, and most modern sensors, displays, flash cards and modes are 3.3V-only, many makers find that they need to perform level shifting/conversion to protect the 3.3V device from 5V. Although one can use resistors to make a divider, for high speed transfers, the resistors can add a lot of slew and cause havoc that is tough to debug. For that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
