# Fritzing sketch shift_74hc299bi_bbbv2 (saved by Fritzing 0.9.3b)
breadboards: 1

parts:
  IC2 = IC, DIP package, 20 pins [chip_label=54HC299]
  BeagleBone1 = BeagleBone Black
  IC1 = IC, DIP package, 20 pins [chip_label=54HC299]
  BeagleBone2 = BeagleBone Black
  U1 = TRANSISTOR_NPN_2 [package=to-92]
  R1 = Resistor [tolerance=±5% resistance=320 package="2512 [SMD]"]
  U2 = TRANSISTOR_NPN_2 [package=to-92]
  R2 = Resistor [tolerance=±5% resistance=320 package="2512 [SMD]"]

nets:
  N1: IC2.pin1, BeagleBone2.no_name_yet#111
  N2: IC2.pin2, IC2.pin3, BeagleBone2.no_name_yet#105
  N3: IC2.pin4, IC1.pin4
  N4: IC2.pin5, IC1.pin5
  N5: IC2.pin6, IC1.pin6
  N6: IC2.pin7, IC1.pin7
  N7: IC2.pin9, BeagleBone2.no_name_yet#115
  N8: IC2.pin10, BeagleBone1.no_name_yet#102, IC1.pin10, BeagleBone2.no_name_yet#1
  N9: IC2.pin11, BeagleBone2.no_name_yet#103
  N10: IC2.pin12, BeagleBone2.no_name_yet#116
  N11: IC2.pin13, IC1.pin13
  N12: IC2.pin14, IC1.pin14
  N13: IC2.pin15, IC1.pin15
  N14: IC2.pin16, IC1.pin16
  N15: IC2.pin17, R2.Pin_1
  N16: IC2.pin19, BeagleBone2.no_name_yet#112
  N17: IC2.pin20, BeagleBone2.no_name_yet#45
  N18: BeagleBone1.no_name_yet#4, U1.E
  N19: BeagleBone1.no_name_yet#8, IC1.pin20
  N20: BeagleBone1.no_name_yet#103, IC1.pin11
  N21: BeagleBone1.no_name_yet#104, U1.C
  N22: BeagleBone1.no_name_yet#105, IC1.pin2, IC1.pin3
  N23: BeagleBone1.no_name_yet#111, IC1.pin19
  N24: BeagleBone1.no_name_yet#112, IC1.pin1
  N25: BeagleBone1.no_name_yet#115, IC1.pin9
  N26: BeagleBone1.no_name_yet#116, IC1.pin12
  N27: BeagleBone1.no_name_yet#121, BeagleBone2.no_name_yet#121
  N28: BeagleBone1.no_name_yet#122, BeagleBone2.no_name_yet#122
  N29: BeagleBone1.no_name_yet#124, BeagleBone2.no_name_yet#124
  N30: IC1.pin17, R1.Pin_1
  N31: BeagleBone2.no_name_yet#5, U2.C
  N32: BeagleBone2.no_name_yet#104, U2.E
  N33: U1.B, R1.Pin_0
  N34: U2.B, R2.Pin_0

notes:
  54hc299 shift register cascaded interface with Beagle Bone Black
  |-8-bit-|

custom parts:
  BeagleBone Black: BeagleBone Black rev. A5B
